# Fritzing sketch jwnode (saved by Fritzing 0.9.3b)
breadboards: 1

parts:
  Part1 = Arduino Uno (Rev3)
  Part2 = Bluetooth HC-05 Macho
  R1 = Resistor [tolerance=±5% resistance=330 package=THT]
  LED1 = LED - 5mm [color="Blue (505nm)" package="5 mm [THT]"]
  U1 = NodeMCU V1.0
  DHT1 = DHT11 Humitidy and Temperature Sensor

nets:
  5V: Part1.5V, Part2.VCC, DHT1.VDD
  GND: Part1.GND, Part2.GND, R1.Pin_0, U1.GND, DHT1.GND
  N1: Part2.TXD, U1.RX
  N2: Part2.RXD, U1.TX
  N3: R1.Pin_1, LED1.anode
  N4: LED1.cathode, U1.D2
  N5: U1.D7, DHT1.DATA

notes:
  Plug the HC-05 in, the short green wires are only pointing to which holes they go in.
  My DHT-11 from Osepp only has 3 pins: +, - and S for Signal. As such I'm able to plug it directly into the breadboard on these 3 holes.

custom parts:
  NodeMCU V1.0: ESP8266 based NodeMCU
  DHT11 Humitidy and Temperature Sensor: DHT11 Humidity and Temperature Sensor
